# Fritzing sketch fan-speed-controller (saved by Fritzing 0.9.9b)
circuit board: 4.44493cm x 4.69541cm
breadboards: 1

parts:
  7805 = Voltage Regulator [package=to220-igo]
  10kΩ = Resistor [tolerance=±5% resistance=1k power=0.25 package=THT]
  Terminal_Block = Camdenboss CTB0158-7 [part_number=CTB0158-7 package=THT]
  1kΩ = Resistor [tolerance=±5% resistance=1k power=0.25 package=THT]
  100nf = Ceramic Capacitor [capacitance=100nF voltage=35V package="100 mil [THT, multilayer]"]
  330nf = Ceramic Capacitor [capacitance=0pF voltage=35V package="100 mil [THT, multilayer]"]
  20kΩ = Resistor [tolerance=±5% resistance=10k power=0.25 package=THT]
  220Ω = Resistor [tolerance=±5% resistance=220 power=0.25 package=THT]
  N-FET = Basic FET N-Channel [package="TO220 [THT]"]
  47nf = Ceramic Capacitor [capacitance=100n voltage=35V package="200 mil [THT, multilayer]"]
  1kΩ_2 = Resistor [tolerance=±5% resistance=10k power=0.25 package=THT]
  1kΩ_3 = Resistor [tolerance=±5% resistance=10k power=0.25 package=THT]
  1kΩ_4 = Resistor [tolerance=±5% resistance=10k power=0.25 package=THT]
  1kΩ_5 = Resistor [tolerance=±5% resistance=10k power=0.25 package=THT]
  ATTINY85 = attiny85 [package=dip]
  Q1 = NPN-Transistor [package="TO92 [THT]"]
  Q2 = NPN-Transistor [package="TO92 [THT]"]
  Q3 = NPN-Transistor [package="TO92 [THT]"]
  Q4 = NPN-Transistor [package="TO92 [THT]"]

nets:
  N1: 7805.GND, Terminal_Block.pin6, 100nf.0, 330nf.0, 20kΩ.Pin_1, 47nf.0, ATTINY85.Pin_4, Q1.E, Q2.E, Q3.E, Q4.E
  N2: 7805.IN, Terminal_Block.pin1, 330nf.1, N-FET.drain
  N3: 7805.OUT, 10kΩ.Pin_1, 100nf.1, ATTINY85.Pin_8
  N4: 10kΩ.Pin_0, ATTINY85.Pin_1
  N5: Terminal_Block.pin2, 1kΩ_2.Pin_0
  N6: Terminal_Block.pin3, 1kΩ_3.Pin_0
  N7: Terminal_Block.pin4, 1kΩ_4.Pin_0
  N8: Terminal_Block.pin5, 1kΩ_5.Pin_0
  N9: Terminal_Block.pin7, 220Ω.Pin_1, 47nf.1
  N10: 1kΩ.Pin_0, 20kΩ.Pin_0, ATTINY85.Pin_3
  N11: 1kΩ.Pin_1, N-FET.gate
  N12: 220Ω.Pin_0, N-FET.source
  N13: 1kΩ_2.Pin_1, Q1.B
  N14: 1kΩ_3.Pin_1, Q2.B
  N15: 1kΩ_4.Pin_1, Q3.B
  N16: 1kΩ_5.Pin_1, Q4.B
  N17: ATTINY85.Pin_2, Q4.C
  N18: ATTINY85.Pin_5, Q3.C
  N19: ATTINY85.Pin_6, Q2.C
  N20: ATTINY85.Pin_7, Q1.C

notes:
  12V
  GND
  OUT
  SW1
  SW2
  SW3
  SW4
  Fan Speed Controller v6.0
  ©2022 That Ain't Working
